# Fritzing sketch Nichoir_main_v2 (saved by Fritzing 0.9.8b)
circuit board: 6.13864cm x 7.87858cm

parts:
  Composant2 = Adafruit Feather M0 Adalogger [part_number="Adafruit #2796"]
  Composant4 = Adafruit MAX31865 RTD Sensor Breakout [part_number="Adafruit #3328"]
  Composant6 = Adafruit DS3231 [part_number="Adafruit #3013"]
  M1 = fc-51 [package=THT]
  M2 = fc-51 [package=THT]
  Servo = Basic Servo
  Q1 = Basic FET N-Channel [package="TO220 [THT]"]
  Q3 = Basic FET N-Channel [package="TO220 [THT]"]
  Q2 = Basic FET N-Channel [package="TO220 [THT]"]
  J4 = double row female pin header, 4 pins [form="♀ (female)"]
  RFID = female pin header, 4 pins [form="♀ (female)"]
  R5 = Resistor [tolerance=±5% power=0.25 resistance=100 package=THT]

nets:
  GND: Composant2.GND, Composant6.GND, Q1.source, Q3.source, Q2.source, J4.pin3, J4.pin4
  N1: Composant2.D1, RFID.pin2
  N2: Composant2.D0, RFID.pin1
  N3: Composant2.MISO, Composant4.SDO
  N4: Composant2.MOSI, Composant4.SDI
  N5: Composant2.SCK, Composant4.SCLK
  N6: Composant2.A5, Q3.gate
  N7: Composant2.A4, Q1.gate
  VIN: Composant2.+3V3, Composant4.VIN, Composant6.Vin, M1.pin3, M2.pin3
  N8: Composant2.VBUS, Servo.vcc, J4.pin1, J4.pin2, RFID.pin3
  N9: Composant2.D12, R5.Pin_0
  N10: Composant2.D11, M1.pin1
  N11: Composant2.D10, M2.pin1
  N12: Composant2.D6, Composant4.CS
  N13: Composant2.D5, Q2.gate
  N14: Composant2.SCL, Composant6.SCL
  N15: Composant2.SDA, Composant6.SDA
  N16: Composant4.GND, M1.pin2, M2.pin2, Q2.drain
  N17: Servo.gnd, Q1.drain
  N18: Servo.pulse, R5.Pin_1
  N19: Q3.drain, RFID.pin4

notes:
  TX
  RX
  5V
  0V
  SG

custom parts:
  Adafruit Feather M0 Adalogger: This is the Adafruit Feather M0 Adalogger - our take on an 'all-in-one' Cortex M0 datalogger (or data-reader) with built in USB and battery charging. Its an Adafruit Feather M0 with a microSD holder ready to rock! We have other boards in the Feather family, check'em out here At the Feather M0's heart is an ATSAMD21G18 ARM Cortex M0 processor, clocked at 48 MHz and at 3.3V logic, the same one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
  Adafruit MAX31865 RTD Sensor Breakout: For precision temperature sensing, nothing beats a Platinum RTD. Resistance temperature detectors (RTDs) are temperature sensors that contain a resistor that changes resistance value as its temperature changes, basically a kind of thermistor. In this sensor, the resistor is actually a small strip of Platinum with a resistance of 100 ohms at 0°C, thus the name PT100. Compared to most NTC/PTC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
  Adafruit DS3231: The datasheet for the DS3231 explains that this part is an "Extremely Accurate I²C-Integrated RTC/TCXO/Crystal". And, hey, it does exactly what it says on the tin! This Real Time Clock (RTC) is the most precise you can get in a small, low power package. Most RTCs use an external 32kHz timing crystal that is used to keep time with low current draw. And that's all well and good, but those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
