# Fritzing sketch Nichoir_power (saved by Fritzing 0.9.9b)
circuit board: 4.07067cm x 6.66048cm

parts:
  Composant9 = PowerBoost 1000 Basic
  Composant11 = Adafruit BQ24074 Solar-DC-USB Lipo Charger
  J3 = double row female pin header, 4 pins [form="♀ (female)"]

nets:
  N1: Composant9.VBAT, Composant11.OUT
  GND: Composant9.GND, Composant11.GND, J3.pin3, J3.pin4
  N2: Composant9.5.0V, J3.pin1, J3.pin2

notes:
  5V
  GND

custom parts:
  PowerBoost 1000 Basic: The PowerBoost 1000 is a little DC/DC boost converter module that can run from 1.8V batteries or higher, and convert the battery output to 5.2V DC for running your 5V projects. At its heart is a TPS61030 boost converter from TI. This boost converter chip has some really nice extras such as low battery detection, 4A internal switch, synchronous conversion, excellent efficiency, and 700KHz high-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
