# Fritzing sketch Nichoir_AntenneIR (saved by Fritzing 0.9.9b)
breadboards: 1

parts:
  IR1 = female pin header, 8 pins [form="♀ (female)"]
  L1 = Inductor [package="0603 [SMD]"]
  IR_Reciever_(TSOP22)1 = IR Reciever
  IR_Reciever_(TSOP22)2 = IR Reciever
  LED1 = LED - 3mm [color="Infrared (940nm)" current=0.030 package="3 mm [THT]"]
  LED2 = LED - 3mm [color="Infrared (940nm)" current=0.030 package="3 mm [THT]"]

nets:
  N1: IR1.pin1, L1.pin_0
  N2: IR1.pin2, L1.pin_1
  N3: IR1.pin3, IR_Reciever_(TSOP22)1.Vs, IR_Reciever_(TSOP22)2.Vs
  GND: IR1.pin4, IR_Reciever_(TSOP22)1.GND, IR_Reciever_(TSOP22)2.GND, LED1.cathode, LED2.cathode
  N4: IR1.pin5, LED1.anode
  N5: IR1.pin6, LED2.anode
  N6: IR1.pin7, IR_Reciever_(TSOP22)1.OUT
  N7: IR1.pin8, IR_Reciever_(TSOP22)2.OUT

custom parts:
  IR Reciever: Basic infrared reciever
