# Fritzing sketch Nichoir_main (saved by Fritzing 0.9.9b)
circuit board: 7.1cm x 7.38cm
breadboards: 1

parts:
  Composant2 = Adafruit Feather M0 Adalogger [part_number="Adafruit #2796"]
  Composant4 = Adafruit MAX31865 RTD Sensor Breakout [part_number="Adafruit #3328"]
  Composant6 = Adafruit DS3231 [part_number="Adafruit #3013"]
  Servo = Basic Servo
  RFID = female pin header, 4 pins [form="♀ (female)"]
  C1 = Electrolytic Capacitor [capacitance=1000µF voltage=10V package="200 mil [THT, electrolytic]"]
  C3 = Electrolytic Capacitor [capacitance=10µF voltage=10V package="100 mil [THT, electrolytic]"]
  C2 = Electrolytic Capacitor [capacitance=10µF voltage=10V package="100 mil [THT, electrolytic]"]
  Ant = female pin header, 2 pins [form="♀ (female)"]
  IR = female pin header, 8 pins [form="♀ (female)"]
  LED = female pin header, 2 pins [form="♀ (female)"]
  R5 = Resistor [tolerance=±5% power=0.25 resistance=100 package=THT]
  PW = double row female pin header, 4 pins [form="♀ (female)"]
  U1 = Voltage Regulator - Variable [package="TO220 [THT]"]
  R9 = Resistor [tolerance=±5% power=0.25 resistance=270 package=THT]
  R8 = Resistor [tolerance=±5% power=0.25 resistance=220 package=THT]
  R7 = Resistor [tolerance=±5% power=0.25 resistance=330 package=THT]
  Q9 = TRANSISTOR_NPN [package=to-92-ammo]
  Q10 = TRANSISTOR_NPN [package=to-92-ammo]
  PW_mng = Header 3 [package=jst-3-pth]
  PW_mng_2 = female pin header, 3 pins [form="♀ (female)"]
  Q12 = Basic FET N-Channel [package="TO220 [THT]"]
  Q13 = Basic FET N-Channel [package="TO220 [THT]"]
  IC1 = Voltage Regulator [package=78xxl]  # not connected

nets:
  GND: Composant2.GND, Composant6.GND, C1.-, PW.pin3, PW.pin4, R9.Pin_1, Q10.E, Q12.source, Q13.source
  N1: Composant2.D1, RFID.pin2
  N2: Composant2.D0, RFID.pin1
  N3: Composant2.MISO, Composant4.SDO
  N4: Composant2.MOSI, Composant4.SDI
  N5: Composant2.SCK, Composant4.SCLK
  N6: Composant2.A5, Q12.gate
  N7: Composant2.A4, Q13.gate
  N8: Composant2.A3, PW_mng.1, PW_mng_2.pin3
  N9: Composant2.A2, PW_mng.2, PW_mng_2.pin2
  N10: Composant2.A1, PW_mng.3, PW_mng_2.pin1
  N11: Composant2.A0, IR.pin1
  +3V3: Composant2.+3V3, Composant6.Vin
  N12: Composant2.VBUS, Servo.vcc, RFID.pin3, C1.+, C2.+, PW.pin1, PW.pin2, U1.IN
  N13: Composant2.D12, R5.Pin_0
  N14: Composant2.D11, Q9.B
  N15: Composant2.D10, IR.pin2
  N16: Composant2.D9, LED.pin1
  N17: Composant2.D6, Composant4.CS
  N18: Composant2.D5, Q10.B
  N19: Composant2.SCL, Composant6.SCL
  N20: Composant2.SDA, Composant6.SDA
  N21: Composant4.VIN, C3.+, IR.pin5, U1.OUT
  N22: Composant4.GND, C3.-, C2.-, IR.pin6, U1.ADJ, Q9.E, Q10.C
  N23: Servo.gnd, Q13.drain
  N24: Servo.pulse, R5.Pin_1
  N25: RFID.pin4, Q12.drain
  N26: Ant.pin1, IR.pin8
  N27: Ant.pin2, IR.pin7
  N28: IR.pin3, R7.Pin_1
  N29: IR.pin4, R8.Pin_1
  N30: LED.pin2, R9.Pin_0
  N31: R8.Pin_0, R7.Pin_0, Q9.C

notes:
  5V
  GND
  Vbat
  B
  A
  0V
  3V3
  IR2
  IR1
  OUT2
  OUT1
  SW
  EN
  TX
  RX
  SG
  + -

custom parts:
  Adafruit Feather M0 Adalogger: This is the Adafruit Feather M0 Adalogger - our take on an 'all-in-one' Cortex M0 datalogger (or data-reader) with built in USB and battery charging. Its an Adafruit Feather M0 with a microSD holder ready to rock! We have other boards in the Feather family, check'em out here At the Feather M0's heart is an ATSAMD21G18 ARM Cortex M0 processor, clocked at 48 MHz and at 3.3V logic, the same one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
  Adafruit MAX31865 RTD Sensor Breakout: For precision temperature sensing, nothing beats a Platinum RTD. Resistance temperature detectors (RTDs) are temperature sensors that contain a resistor that changes resistance value as its temperature changes, basically a kind of thermistor. In this sensor, the resistor is actually a small strip of Platinum with a resistance of 100 ohms at 0°C, thus the name PT100. Compared to most NTC/PTC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
  Adafruit DS3231: The datasheet for the DS3231 explains that this part is an "Extremely Accurate I²C-Integrated RTC/TCXO/Crystal". And, hey, it does exactly what it says on the tin! This Real Time Clock (RTC) is the most precise you can get in a small, low power package. Most RTCs use an external 32kHz timing crystal that is used to keep time with low current draw. And that's all well and good, but those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
