# Fritzing sketch Nichoir_power (saved by Fritzing 0.9.9b)
circuit board: 4.07067cm x 6.66048cm

parts:
  C3 = Ceramic Capacitor [capacitance=0.1µF voltage=35V package="100 mil [THT, multilayer]"]
  PW = double row female pin header, 4 pins [form="♀ (female)"]
  C2 = Ceramic Capacitor [capacitance=1µF voltage=35V package="100 mil [THT, multilayer]"]
  C4 = Electrolytic Capacitor [capacitance=1mF voltage=35V package="200 mil [THT, electrolytic]"]
  Solar/DC/USB_Lipo_charger = Generic female header - 11 pins [form="♀ (female)" package=THT]
  Switch = female pin header, 2 pins [form="♀ (female)"]
  PW_mng = Generic female header - 3 pins [form="♀ (female)" package=THT]
  Power_Boost = Generic female header - 6 pins [form="♀ (female)" package=THT]
  D1 = Rectifier Diode [part_number=1N4001 package="300 mil [THT]"]
  D2 = Rectifier Diode [part_number=1N4001 package="300 mil [THT]"]
  R6 = Resistor [tolerance=±5% resistance=47k power=0.25 package="1206 [SMD]"]
  R5 = Resistor [tolerance=±5% resistance=10k power=0.25 package="1206 [SMD]"]
  R4 = Resistor [tolerance=±5% resistance=100k package="1206 [SMD]"]
  R3 = Resistor [tolerance=±5% resistance=100k package="1206 [SMD]"]
  R1 = Resistor [tolerance=±5% resistance=100k package="1206 [SMD]"]
  R2 = Resistor [tolerance=±5% resistance=100k package="1206 [SMD]"]

nets:
  N1: C3.0, Switch.pin1, D1.anode, D2.anode
  N2: C3.1, C4.+, Solar/DC/USB_Lipo_charger.OUT, Switch.pin2, Power_Boost.Vbat, R1.Pin_0
  N3: PW.pin1, PW.pin2, Power_Boost.5V
  GND: PW.pin3, PW.pin4, C2.0, C4.-, Solar/DC/USB_Lipo_charger.GND#8, Power_Boost.GND#4, R4.Pin_1, R3.Pin_1, R2.Pin_1
  N4: C2.1, PW_mng.Vbat, R1.Pin_1, R2.Pin_0
  N5: PW_mng.EN, R6.Pin_1
  N6: PW_mng.BUT, R5.Pin_1
  N7: Power_Boost.EN, D2.cathode, R6.Pin_0, R4.Pin_0
  N8: D1.cathode, R5.Pin_0, R3.Pin_0

notes:
  5V
  GND
  Vbat
  EN
  SW
  LBO
  Gnd
  OUT
  Lipo

custom parts:
  Generic female header - 11 pins: Generic female header
  Generic female header - 3 pins: Generic female header
  Generic female header - 6 pins: Generic female header
